// Logisim project Trabalho_1_herickBittencourt.circ as structural Verilog: 2 circuits, main circuit main
module main (
  input  A2,
  input  A1,
  input  A0
);

  wire decodificador_1_l1, decodificador_1_l2, decodificador_1_l3, decodificador_1_l4, decodificador_1_l5,
       decodificador_1_l6, decodificador_1_l7;

  decodificador decodificador_1 (
    .a2(A2), .a1(A1), .a0(A0), .L1(decodificador_1_l1), .L2(decodificador_1_l2), .L3(decodificador_1_l3),
    .L4(decodificador_1_l4), .L5(decodificador_1_l5), .L6(decodificador_1_l6), .L7(decodificador_1_l7));
  LED L1 (.in(decodificador_1_l1));
  LED L3 (.in(decodificador_1_l3));
  LED L6 (.in(decodificador_1_l6));
  LED L2 (.in(decodificador_1_l2));
  LED L4 (.in(decodificador_1_l4));
  LED L5 (.in(decodificador_1_l5));
  LED L7 (.in(decodificador_1_l7));
endmodule

module decodificador (
  input  a2,
  input  a1,
  input  a0,
  output L1,
  output L2,
  output L3,
  output L4,
  output L5,
  output L6,
  output L7
);

  or or_1 (L1, a1, a2);
  and and_1 (L3, a2, a1);
  and and_2 (L5, a2, a1);
  or or_2 (L7, a1, a2);

  assign L2 = a2;
  assign L4 = a0;
  assign L6 = a2;
endmodule
