// Logisim project ULA_HerickBittencourt.circ as structural Verilog: 14 circuits, main circuit main
module main (
  input  [3:0] A,
  input  [3:0] B,
  input  [2:0] SEL,
  output OF,
  output ZF,
  output [3:0] out_6,
  output Sinal
);

  wire [3:0] display_complemento_2_1_s;

  Display_Complemento_2 display_complemento_2_1 (.S(display_complemento_2_1_s), .in_1(out_6), .Sinal(Sinal));
  ULA ula_1 (.SEL(SEL), .OF(OF), .ZF(ZF), .A(A), .B(B), .out_5(out_6));
  Hex_Digit_Display hex_digit_display_1 (.value(display_complemento_2_1_s));  // open: dp

  // Notes on the sheet:
  //   Opções de seletor:
  //   0 - Pass A
  //   1 - A - 1 (Decremento)
  //   2 - A + 1 (Incremento)
  //   3 - A + B
  //   4 - A - B
  //   5 - NOT Bitwise A
  //   6 - OR Bitwise
  //   7 - AND Bitwise
endmodule

module ULA (
  input  [3:0] A,
  input  [3:0] B,
  input  [2:0] SEL,
  output OF,
  output [3:0] out_5,
  output ZF
);

  wire decrementador_1_out_3, incrementador_1_out_3, somador_4_bits_1_of, subtrator_4_bits_1_out_4;
  wire [3:0] and_bitwise_1_out_3, decrementador_1_out_4, incrementador_1_out_4, not_bitwise_1_out_2,
       or_bitwise_1_out_3, somador_4_bits_1_s, subtrator_4_bits_1_out_5;

  Decrementador decrementador_1 (
    .in_1(A), .out_3(decrementador_1_out_3), .out_4(decrementador_1_out_4));  // open: out_2
  Incrementador incrementador_1 (
    .in_1(A), .out_4(incrementador_1_out_4), .out_3(incrementador_1_out_3));  // open: out_2
  Somador_4_Bits somador_4_bits_1 (
    .OF(somador_4_bits_1_of), .Cin(1'b0), .A(A), .B(B), .S(somador_4_bits_1_s));  // open: Cout
  Multiplexer #(.select(3), .width(4), .enable("false")) multiplexer_1 (
    .in0(A), .in1(decrementador_1_out_4), .in2(incrementador_1_out_4), .in3(somador_4_bits_1_s),
    .in4(subtrator_4_bits_1_out_5), .in5(not_bitwise_1_out_2), .in6(or_bitwise_1_out_3),
    .in7(and_bitwise_1_out_3), .out(out_5), .sel(SEL));
  Zero_Check zero_check_1 (.out_2(ZF), .in_1(out_5));
  Subtrator_4_Bits subtrator_4_bits_1 (
    .A(A), .B(B), .out_5(subtrator_4_bits_1_out_5), .out_4(subtrator_4_bits_1_out_4));  // open: out_3
  NOT_Bitwise not_bitwise_1 (.A(A), .out_2(not_bitwise_1_out_2));
  OR_Bitwise or_bitwise_1 (.A(A), .B(B), .out_3(or_bitwise_1_out_3));
  Overflow_Check overflow_check_1 (
    .in_1(decrementador_1_out_3), .out_6(OF), .in_2(incrementador_1_out_3), .in_3(somador_4_bits_1_of),
    .in_4(subtrator_4_bits_1_out_4), .in_5(SEL));
  AND_Bitwise and_bitwise_1 (.A(A), .B(B), .out_3(and_bitwise_1_out_3));
endmodule

module Meio_Somador (
  input  A0,
  input  B0,
  output Cout,
  output S
);

  and and_1 (Cout, A0, B0);
  xor xor_1 (S, A0, B0);
endmodule

module Somador (
  input  A0,
  input  B0,
  input  Cin,
  output Cout,
  output S
);

  wire and_1_out, meio_somador_1_cout, meio_somador_1_s;

  or or_1 (Cout, meio_somador_1_cout, and_1_out);
  and and_1 (and_1_out, meio_somador_1_s, Cin);
  Meio_Somador meio_somador_1 (.Cout(meio_somador_1_cout), .S(meio_somador_1_s), .A0(A0), .B0(B0));
  xor xor_1 (S, Cin, meio_somador_1_s);
endmodule

module Somador_4_Bits (
  input  [3:0] A,
  input  [3:0] B,
  input  Cin,
  output Cout,
  output [3:0] S,
  output OF
);

  wire somador_2_cout, somador_3_cout, somador_4_cout;

  xor xor_1 (OF, Cout, somador_2_cout);
  Somador somador_1 (.Cin(somador_2_cout), .A0(A[3]), .B0(B[3]), .Cout(Cout), .S(S[3]));
  Somador somador_2 (.Cin(somador_3_cout), .A0(A[2]), .B0(B[2]), .Cout(somador_2_cout), .S(S[2]));
  Somador somador_3 (.Cin(somador_4_cout), .A0(A[1]), .B0(B[1]), .Cout(somador_3_cout), .S(S[1]));
  Somador somador_4 (.Cin(Cin), .A0(A[0]), .B0(B[0]), .Cout(somador_4_cout), .S(S[0]));
endmodule

module Incrementador (
  input  [3:0] in_1,
  output out_2,
  output out_3,
  output [3:0] out_4
);

  Somador_4_Bits somador_4_bits_1 (.Cout(out_2), .OF(out_3), .Cin(1'b0), .A(in_1), .B(4'b0001), .S(out_4));
endmodule

module Decrementador (
  input  [3:0] in_1,
  output out_2,
  output out_3,
  output [3:0] out_4
);

  Somador_4_Bits somador_4_bits_1 (.Cout(out_2), .OF(out_3), .Cin(1'b0), .A(in_1), .B(4'b1111), .S(out_4));
endmodule

module Subtrator_4_Bits (
  input  [3:0] B,
  input  [3:0] A,
  output out_3,
  output out_4,
  output [3:0] out_5
);

  wire [3:0] not_1_out;

  assign not_1_out = ~B;  // NOT_Gate not_1, 4 bits wide
  Somador_4_Bits somador_4_bits_1 (.Cout(out_3), .OF(out_4), .Cin(1'b1), .A(A), .B(not_1_out), .S(out_5));
endmodule

module NOT_Bitwise (
  input  [3:0] A,
  output [3:0] out_2
);

  assign out_2 = ~A;  // NOT_Gate not_1, 4 bits wide
endmodule

module AND_Bitwise (
  input  [3:0] A,
  input  [3:0] B,
  output [3:0] out_3
);

  and and_1 (out_3[2], A[2], B[2]);
  and and_2 (out_3[3], A[3], B[3]);
  and and_3 (out_3[0], A[0], B[0]);
  and and_4 (out_3[1], A[1], B[1]);
endmodule

module OR_Bitwise (
  input  [3:0] A,
  input  [3:0] B,
  output [3:0] out_3
);

  or or_1 (out_3[2], A[2], B[2]);
  or or_2 (out_3[3], A[3], B[3]);
  or or_3 (out_3[1], A[1], B[1]);
  or or_4 (out_3[0], A[0], B[0]);
endmodule

module Overflow_Check (
  input  in_1,
  input  in_2,
  input  in_3,
  input  in_4,
  input  [2:0] in_5,
  output out_6
);

  Multiplexer #(.select(3), .enable("false")) multiplexer_1 (
    .in0(1'b0), .in1(in_1), .in2(in_2), .in3(in_3), .in4(in_4), .in5(1'b0), .in6(1'b0), .in7(1'b0),
    .out(out_6), .sel(in_5));
endmodule

module Zero_Check (
  input  [3:0] in_1,
  output out_2
);

  Comparator #(.width(4), .mode("unsigned")) comparator_1 (.a(in_1), .b(4'b0000), .eq(out_2));  // open: gt, lt
endmodule

module Display_Complemento_2 (
  input  [3:0] in_1,
  output Sinal,
  output [3:0] S
);

  wire [3:0] incrementador_1_out_4, not_bitwise_1_out_2;

  NOT_Bitwise not_bitwise_1 (.A(in_1), .out_2(not_bitwise_1_out_2));
  Incrementador incrementador_1 (.in_1(not_bitwise_1_out_2), .out_4(incrementador_1_out_4));  // open: out_3, out_2
  Multiplexer #(.width(4), .enable("false")) multiplexer_1 (
    .in0(in_1), .in1(incrementador_1_out_4), .out(S), .sel(in_1[3]));

  assign Sinal = in_1[3];
endmodule
