// Logisim project GeradorSequencia_herickBittencourt.circ as structural Verilog: 7 circuits, main circuit main
module main (
  output out_1
);

  wire clock_1_out;
  wire [3:0] contadorfinal_1_out_2;

  Clock clock_1 (.out(clock_1_out));
  ContadorFinal contadorfinal_1 (.CLK(clock_1_out), .out_2(contadorfinal_1_out_2), .ContAtual(out_1));
  Hex_Digit_Display hex_digit_display_1 (.value(contadorfinal_1_out_2));  // open: dp

  // Notes on the sheet:
  //   (pode levar 1 ciclo em cada um até se ajustar e entrar no loop)
  //   Trabalho M3 Circuitos Digitais
  //   Aluno: Hérick Vitor Vieira Bittencourt
  //   Contador primário:
  //   [7 -> 11 -> 8 -> 13 -> 10 -> 15 -> 14 -> 5 -> 4 -> 3]
  //   [7 -> B  -> 8 -> D  -> A  -> F  -> E  -> 5 -> 4 -> 3]
  //   Contador auxiliar:
  //   [1 -> 3 -> 14 -> 7 -> 15 -> 13 -> 9 -> 4 -> 5 -> 10]
  //   [1 -> 3 -> E  -> 7 -> F  -> D  -> 9 -> 4 -> 5 -> A]
  //   Contador atual:
  //   0 = Primario
  //   1 = Auxiliar
endmodule

module Contador1 (
  input  CLK,
  output [3:0] out_2
);

  wire contador1_circuito_1_t0, contador1_circuito_1_t1, contador1_circuito_1_t2, contador1_circuito_1_t3;

  Contador1_Circuito contador1_circuito_1 (
    .Q3____Q0(out_2), .T3(contador1_circuito_1_t3), .T2(contador1_circuito_1_t2),
    .T1(contador1_circuito_1_t1), .T0(contador1_circuito_1_t0));
  T_Flip_Flop _3 (.clk(CLK), .T(contador1_circuito_1_t3), .Q(out_2[3]));  // open: Qn, preset, reset, en
  Hex_Digit_Display hex_digit_display_1 (.value(out_2));  // open: dp
  T_Flip_Flop _2 (.clk(CLK), .T(contador1_circuito_1_t2), .Q(out_2[2]));  // open: Qn, preset, reset, en
  T_Flip_Flop _1 (.clk(CLK), .T(contador1_circuito_1_t1), .Q(out_2[1]));  // open: Qn, preset, reset, en
  T_Flip_Flop _0 (.clk(CLK), .T(contador1_circuito_1_t0), .Q(out_2[0]));  // open: Qn, preset, reset, en

  // Notes on the sheet:
  //   [7 -> 11 -> 8 -> 13 -> 10 -> 15 -> 14 -> 5 -> 4 -> 3]
  //   [7 -> B  -> 8 -> D  -> A  -> F  -> E  -> 5 -> 4 -> 3]
  //   CONTADOR PRINCIPAL
  //   Hérick Bittencourt
endmodule

module Contador1_Circuito (
  input  [3:0] Q3____Q0,
  output T3,
  output T2,
  output T1,
  output T0
);

  wire and_1_out, and_2_out, and_3_out, and_4_out, and_5_out, and_6_out, and_7_out, and_8_out, and_9_out,
       and_10_out, and_11_out, and_12_out, and_13_out, not_1_out, not_2_out, not_3_out, not_4_out, not_5_out,
       not_6_out, not_7_out, not_8_out, not_9_out, not_10_out, not_11_out, not_12_out, or_2_out, or_3_out,
       or_6_out;

  not not_1 (not_1_out, Q3____Q0[3]);
  not not_2 (not_2_out, Q3____Q0[3]);
  not not_3 (not_3_out, Q3____Q0[0]);
  not not_4 (not_4_out, Q3____Q0[2]);
  not not_5 (not_5_out, Q3____Q0[0]);
  not not_6 (not_6_out, Q3____Q0[3]);
  not not_7 (not_7_out, Q3____Q0[1]);
  not not_8 (not_8_out, Q3____Q0[2]);
  not not_9 (not_9_out, Q3____Q0[1]);
  and and_1 (and_1_out, not_1_out, Q3____Q0[2]);
  and and_2 (and_2_out, Q3____Q0[3], Q3____Q0[2]);
  not not_10 (not_10_out, Q3____Q0[0]);
  and and_3 (and_3_out, not_2_out, not_3_out);
  and and_4 (and_4_out, not_4_out, not_5_out);
  and and_5 (and_5_out, not_6_out, Q3____Q0[1]);
  and and_6 (and_6_out, Q3____Q0[3], not_7_out);
  not not_11 (not_11_out, Q3____Q0[0]);
  and and_7 (and_7_out, Q3____Q0[3], not_8_out);
  or or_1 (T0, not_9_out, Q3____Q0[3]);
  and and_8 (and_8_out, and_1_out, Q3____Q0[1]);
  and and_9 (and_9_out, and_2_out, not_10_out);
  or or_2 (or_2_out, and_3_out, and_4_out);
  or or_3 (or_3_out, and_5_out, and_6_out);
  and and_10 (and_10_out, Q3____Q0[2], not_11_out);
  and and_11 (and_11_out, and_7_out, Q3____Q0[0]);
  and and_12 (and_12_out, Q3____Q0[3], Q3____Q0[2]);
  not not_12 (not_12_out, Q3____Q0[1]);
  or or_4 (T3, and_8_out, and_9_out);
  or or_5 (T2, or_2_out, or_3_out);
  or or_6 (or_6_out, and_10_out, and_11_out);
  and and_13 (and_13_out, and_12_out, not_12_out);
  or or_7 (T1, or_6_out, and_13_out);
endmodule

module Contador2 (
  input  CLK,
  output [3:0] out_2
);

  wire contador2_circuito_1_t0, contador2_circuito_1_t1, contador2_circuito_1_t2, contador2_circuito_1_t3;

  Contador2_Circuito contador2_circuito_1 (
    .Q3____Q0(out_2), .T3(contador2_circuito_1_t3), .T2(contador2_circuito_1_t2),
    .T1(contador2_circuito_1_t1), .T0(contador2_circuito_1_t0));
  T_Flip_Flop _3 (.clk(CLK), .T(contador2_circuito_1_t3), .Q(out_2[3]));  // open: Qn, preset, reset, en
  Hex_Digit_Display hex_digit_display_1 (.value(out_2));  // open: dp
  T_Flip_Flop _2 (.clk(CLK), .T(contador2_circuito_1_t2), .Q(out_2[2]));  // open: Qn, preset, reset, en
  T_Flip_Flop _1 (.clk(CLK), .T(contador2_circuito_1_t1), .Q(out_2[1]));  // open: Qn, preset, reset, en
  T_Flip_Flop _0 (.clk(CLK), .T(contador2_circuito_1_t0), .Q(out_2[0]));  // open: Qn, preset, reset, en

  // Notes on the sheet:
  //   [1 -> 3 -> 14 -> 7 -> 15 -> 13 -> 9 -> 4 -> 5 -> 10]
  //   [1 -> 3 -> E  -> 7 -> F  -> D  -> 9 -> 4 -> 5 -> A]
  //   CONTADOR AUXILIAR
endmodule

module Contador2_Circuito (
  input  [3:0] Q3____Q0,
  output T3,
  output T2,
  output T1,
  output T0
);

  wire and_1_out, and_2_out, and_3_out, and_4_out, and_5_out, and_6_out, and_7_out, and_8_out, and_9_out,
       and_10_out, and_11_out, and_12_out, and_13_out, and_14_out, and_15_out, and_16_out, and_17_out,
       and_18_out, and_19_out, not_1_out, not_2_out, not_3_out, not_4_out, not_5_out, not_6_out, not_7_out,
       not_8_out, not_9_out, not_10_out, not_11_out, not_12_out, not_13_out, not_14_out, not_15_out,
       not_16_out, not_17_out, or_1_out, or_2_out, or_3_out, or_4_out, or_5_out, or_6_out;

  not not_1 (not_1_out, Q3____Q0[3]);
  not not_2 (not_2_out, Q3____Q0[3]);
  not not_3 (not_3_out, Q3____Q0[2]);
  not not_4 (not_4_out, Q3____Q0[1]);
  not not_5 (not_5_out, Q3____Q0[3]);
  not not_6 (not_6_out, Q3____Q0[1]);
  not not_7 (not_7_out, Q3____Q0[3]);
  not not_8 (not_8_out, Q3____Q0[3]);
  and and_1 (and_1_out, not_1_out, Q3____Q0[2]);
  not not_9 (not_9_out, Q3____Q0[2]);
  not not_10 (not_10_out, Q3____Q0[0]);
  and and_2 (and_2_out, not_2_out, not_3_out);
  and and_3 (and_3_out, Q3____Q0[2], not_4_out);
  not not_11 (not_11_out, Q3____Q0[2]);
  not not_12 (not_12_out, Q3____Q0[0]);
  and and_4 (and_4_out, not_5_out, not_6_out);
  not not_13 (not_13_out, Q3____Q0[2]);
  and and_5 (and_5_out, not_7_out, Q3____Q0[2]);
  not not_14 (not_14_out, Q3____Q0[1]);
  not not_15 (not_15_out, Q3____Q0[2]);
  and and_6 (and_6_out, not_8_out, Q3____Q0[1]);
  and and_7 (and_7_out, and_1_out, Q3____Q0[0]);
  and and_8 (and_8_out, Q3____Q0[3], not_9_out);
  and and_9 (and_9_out, Q3____Q0[3], not_10_out);
  and and_10 (and_10_out, and_2_out, Q3____Q0[1]);
  and and_11 (and_11_out, and_3_out, Q3____Q0[0]);
  not not_16 (not_16_out, Q3____Q0[1]);
  and and_12 (and_12_out, not_11_out, not_12_out);
  and and_13 (and_13_out, and_4_out, Q3____Q0[0]);
  and and_14 (and_14_out, Q3____Q0[3], Q3____Q0[1]);
  not not_17 (not_17_out, Q3____Q0[0]);
  and and_15 (and_15_out, not_13_out, Q3____Q0[1]);
  and and_16 (and_16_out, and_5_out, not_14_out);
  and and_17 (and_17_out, Q3____Q0[3], not_15_out);
  or or_1 (or_1_out, and_6_out, and_7_out);
  or or_2 (or_2_out, and_8_out, and_9_out);
  or or_3 (or_3_out, and_10_out, and_11_out);
  and and_18 (and_18_out, Q3____Q0[3], not_16_out);
  or or_4 (or_4_out, and_12_out, and_13_out);
  and and_19 (and_19_out, and_14_out, Q3____Q0[0]);
  or or_5 (or_5_out, not_17_out, and_15_out);
  or or_6 (or_6_out, and_16_out, and_17_out);
  or or_7 (T3, or_1_out, or_2_out);
  or or_8 (T2, or_3_out, and_18_out);
  or or_9 (T1, or_4_out, and_19_out);
  or or_10 (T0, or_5_out, or_6_out);
endmodule

module ContadorFinal (
  input  CLK,
  output [3:0] out_2,
  output ContAtual
);

  wire and_1_out, and_2_out, demultiplexer_1_out0, demultiplexer_1_out1, verificadorcontagem_1_debouncea,
       verificadorcontagem_1_debounceb;
  wire [3:0] contador1_1_out_2, contador2_1_out_2;

  Demultiplexer #(.enable("false")) demultiplexer_1 (
    .out0(demultiplexer_1_out0), .out1(demultiplexer_1_out1), .in(CLK), .sel(ContAtual));
  VerificadorContagem verificadorcontagem_1 (
    .Q1(contador1_1_out_2), .Q2(contador2_1_out_2), .out_4(ContAtual),
    .DebounceB(verificadorcontagem_1_debounceb), .DebounceA(verificadorcontagem_1_debouncea), .CLK(CLK));
  and and_1 (and_1_out, demultiplexer_1_out0, ~verificadorcontagem_1_debouncea);  // AND_Gate
  Hex_Digit_Display hex_digit_display_1 (.value(contador1_1_out_2));  // open: dp
  Contador1 contador1_1 (.CLK(and_1_out), .out_2(contador1_1_out_2));
  and and_2 (and_2_out, demultiplexer_1_out1, ~verificadorcontagem_1_debounceb);  // AND_Gate
  Hex_Digit_Display hex_digit_display_2 (.value(contador2_1_out_2));  // open: dp
  Contador2 contador2_1 (.CLK(and_2_out), .out_2(contador2_1_out_2));
  Multiplexer #(.width(4), .enable("false")) multiplexer_1 (
    .in0(contador1_1_out_2), .in1(contador2_1_out_2), .out(out_2), .sel(ContAtual));
  Hex_Digit_Display hex_digit_display_3 (.value(out_2));  // open: dp
endmodule

module VerificadorContagem (
  input  [3:0] Q1,
  input  [3:0] Q2,
  input  CLK,
  output out_4,
  output DebounceB,
  output DebounceA
);

  wire A_q, and_1_out, B_q, comparator_1_eq, comparator_2_eq, comparator_3_eq, or_1_out;

  Comparator #(.width(4), .mode("unsigned")) comparator_1 (.a(Q1), .b(4'b0011), .eq(comparator_1_eq));  // open: gt, lt
  Comparator #(.width(4), .mode("unsigned")) comparator_2 (.a(Q2), .b(4'b1010), .eq(comparator_2_eq));  // open: gt, lt
  or or_1 (or_1_out, comparator_1_eq, comparator_2_eq);
  D_Flip_Flop A (.clk(CLK), .D(or_1_out), .Q(A_q));  // open: Qn, preset, en, reset
  T_Flip_Flop #(.trigger("falling")) t_ff_1 (.clk(or_1_out), .T(1'b1), .Q(out_4));  // open: Qn, preset, reset, en
  D_Flip_Flop B (.clk(CLK), .D(out_4), .Q(B_q));  // open: Qn, preset, en, reset
  and and_1 (and_1_out, A_q, B_q);
  Comparator #(.width(1)) comparator_3 (.a(B_q), .b(A_q), .gt(DebounceB), .eq(comparator_3_eq));  // open: lt
  and and_2 (DebounceA, comparator_3_eq, and_1_out);

  // Notes on the sheet:
  //   A = 1 e B = 0 indica que Cont. Aux será acionado
  //   A = 1 e B = 1 indica que Cont. Primario será acionado
  //   Como o CLK aumenta qualquer contador
  //   se passar p/ ele, é necessário detectar
  //   a troca de contador p/ travar o circuito
  //   recem-ativado de aumentar simultaneamente
  //   com o anterior
endmodule
